# Fritzing sketch HardwareSchema (saved by Fritzing 0.8.7b)
breadboards: 1

parts:
  Raspberry_Pi_1 = Raspberry Pi 4 [part_number=RPI-4-b]
  S1 = Pushbutton [package="[THT]"]
  S2 = Pushbutton [package="[THT]"]
  R1 = Resistor [tolerance=±5% resistance=220 package=THT]
  R2 = Resistor [tolerance=±5% resistance=220 package=THT]
  IC1 = MCP3008 8-channel 10-bit ADC [part_number=MCP3008]
  R3 = Resistor [tolerance=±5% resistance=220 package=THT]
  Part2 = Black Joystick KY-023

nets:
  3V3: Raspberry_Pi_1.3v3, IC1.no_name_yet#7, IC1.no_name_yet#8, R3.Pin_1, Part2.+5V
  N1: Raspberry_Pi_1.GPIO10, IC1.no_name_yet#3
  N2: Raspberry_Pi_1.GPIO9, IC1.no_name_yet#4
  N3: Raspberry_Pi_1.GPIO11, IC1.no_name_yet#5
  N4: Raspberry_Pi_1.GPIO26, S1.Pin_3, S1.Pin_4
  N5: Raspberry_Pi_1.GPIO20, S2.Pin_3, S2.Pin_4
  N6: Raspberry_Pi_1.GPIO8, IC1.no_name_yet#2
  GND: Raspberry_Pi_1.GND, R1.Pin_1, R2.Pin_1, IC1.no_name_yet#6, Part2.GND
  N7: S1.Pin_1, S1.Pin_2, R1.Pin_0
  N8: S2.Pin_1, S2.Pin_2, R2.Pin_0
  N9: IC1.no_name_yet#9, R3.Pin_0, Part2.SW
  N10: IC1.no_name_yet#10, Part2.VRx
  N11: IC1.no_name_yet#11, Part2.VRy

custom parts:
  Raspberry Pi 4: The RPi4, a faster version of the awesome Raspberry Pi 2 B ARM Board with 40 pin gpio. Ready for special Raspberry Pi B+ and RPi2 Hat (Hardware attached (on) top)
  Black Joystick KY-023: Description: The joystick is a combination of 2 analoog potentiometer and a digital switch. Arduino GND --> Module pin - Arduino +5V --> Module pin +5V Arduino Analoog 0 --> Module VRx Arduino Analoog 1 --> Module VRy Arduino Digital --> Module SW Dimensions: 1" x 1.25"
